// Logisim project 32-bit CPU.circ as structural Verilog: 9 circuits, main circuit CPU
module CPU (
  input  Write,
  input  [31:0] in_val,
  input  [3:0] Rd,
  input  [3:0] Ra,
  input  [3:0] Rb,
  input  Sub,
  input  [2:0] Op,
  input  [31:0] A,
  input  [31:0] B,
  input  in_10,
  output [31:0] out_a,
  output [31:0] out_b,
  output [31:0] R,
  output Zero
);

  wire clk_out, clock_1_out, clock_2_out, clock_3_out, clock_4_out, Data, demultiplexer_1_out0,
       demultiplexer_1_out1, demultiplexer_1_out2, demultiplexer_1_out3, demultiplexer_1_out4,
       demultiplexer_1_out5, demultiplexer_1_out6, demultiplexer_1_out7, demultiplexer_1_out8,
       demultiplexer_1_out9, demultiplexer_1_out10, demultiplexer_1_out11, demultiplexer_1_out12,
       demultiplexer_1_out13, demultiplexer_1_out14, demultiplexer_1_out15, Load, LoadL, n1b_alu_1_cout,
       n1b_alu_2_cout, n1b_alu_3_cout, n1b_alu_4_cout, n1b_alu_5_cout, n1b_alu_6_cout, n1b_alu_7_cout,
       n1b_alu_8_cout, n1b_alu_9_cout, n1b_alu_10_cout, n1b_alu_11_cout, n1b_alu_12_cout, n1b_alu_13_cout,
       n1b_alu_14_cout, n1b_alu_15_cout, n1b_alu_16_cout, n1b_alu_17_cout, n1b_alu_18_cout, n1b_alu_19_cout,
       n1b_alu_20_cout, n1b_alu_21_cout, n1b_alu_22_cout, n1b_alu_23_cout, n1b_alu_24_cout, n1b_alu_25_cout,
       n1b_alu_26_cout, n1b_alu_27_cout, n1b_alu_28_cout, n1b_alu_29_cout, n1b_alu_30_cout, n1b_alu_31_cout,
       n1b_alu_32_out_9, not_1_out, or_1_out, Store, undriven, undriven_2, undriven_3, undriven_4,
       undriven_5, undriven_6, undriven_7;
  wire [3:0] bit_extender_5_out;
  wire [7:2] Addr;
  wire [15:0] bit_extender_1_out, bit_extender_3_out, multiplexer_1_out, Program_Counter_q;
  wire [31:0] bit_extender_4_out, Instruction_Format__32_Bit_q31, Instruction_Register_q, R0_q, R1_q, R2_q,
       R3_q, R4_q, R5_q, R6_q, R7_q, R8_q, R9_q, R10_q, R11_q, R12_q, R13_q, R14_q, R15_q, ram_1_data,
       ram_2_data, ram_3_data, undriven_8;

  Bit_Extender #(.in_width(32)) bit_extender_1 (.in(undriven_8), .out(bit_extender_1_out));
  Multiplexer #(.width(16), .enable("false")) multiplexer_1 (
    .in0(bit_extender_1_out), .in1(Program_Counter_q), .out(multiplexer_1_out), .sel(undriven));
  assign A = {{31{1'b0}}, undriven};  // Bit_Extender bit_extender_2
  // Probe on multiplexer_1_out
  not not_1 (not_1_out, Load);
  Clock clock_1 (.out(clock_1_out));
  RAM #(.addrWidth(16), .dataWidth(32), .bus("separate")) ram_1 (
    .addr(multiplexer_1_out), .din(ram_2_data), .data(ram_1_data), .str(not_1_out), .sel(Zero),
    .clk(clock_1_out), .ld(Load), .clr(1'b0));
  assign bit_extender_3_out = {{8{1'b0}}, {Addr[7:5], {2{Addr[5]}}, {3{Addr[2]}}}};  // Bit_Extender bit_extender_3
  // Probe on ram_1_data
  Clock clock_2 (.out(clock_2_out));
  Counter #(.width(16), .max('hffff)) Program_Counter (
    .Q(Program_Counter_q), .clk(clock_3_out));  // open: load, D, count, carry, clr
  Clock clock_3 (.out(clock_3_out));
  RAM #(.addrWidth(16), .dataWidth(32), .bus("separate")) ram_2 (
    .addr(bit_extender_3_out), .din(ram_1_data), .data(ram_2_data), .str(Store), .clk(clock_2_out), .ld(Load));  // open: sel, clr
  Shift_Register #(.length(32)) Instruction_Format__32_Bit (
    .in(1'b1), .clk(1'b1), .load(undriven_2), .q0(Instruction_Format__32_Bit_q31[31]),
    .q1(Instruction_Format__32_Bit_q31[30]), .q2(Instruction_Format__32_Bit_q31[29]), .d3(undriven_2),
    .q3(Instruction_Format__32_Bit_q31[28]), .d4(undriven_3), .q4(Instruction_Format__32_Bit_q31[27]),
    .d5(undriven_4), .q5(Instruction_Format__32_Bit_q31[26]), .q6(Instruction_Format__32_Bit_q31[25]),
    .q7(Instruction_Format__32_Bit_q31[24]), .d8(undriven_4), .q8(Instruction_Format__32_Bit_q31[23]),
    .d9(undriven_5), .q9(Instruction_Format__32_Bit_q31[22]), .q10(Instruction_Format__32_Bit_q31[21]),
    .q11(Instruction_Format__32_Bit_q31[20]), .d12(undriven_5), .q12(Instruction_Format__32_Bit_q31[19]),
    .d13(undriven_6), .q13(Instruction_Format__32_Bit_q31[18]), .q14(Instruction_Format__32_Bit_q31[17]),
    .q15(Instruction_Format__32_Bit_q31[16]), .q16(Instruction_Format__32_Bit_q31[15]),
    .q17(Instruction_Format__32_Bit_q31[14]), .q18(Instruction_Format__32_Bit_q31[13]),
    .q19(Instruction_Format__32_Bit_q31[12]), .q20(Instruction_Format__32_Bit_q31[11]),
    .q21(Instruction_Format__32_Bit_q31[10]), .q22(Instruction_Format__32_Bit_q31[9]),
    .q23(Instruction_Format__32_Bit_q31[8]), .q24(Instruction_Format__32_Bit_q31[7]),
    .q25(Instruction_Format__32_Bit_q31[6]), .q26(Instruction_Format__32_Bit_q31[5]),
    .q27(Instruction_Format__32_Bit_q31[4]), .q28(Instruction_Format__32_Bit_q31[3]),
    .q29(Instruction_Format__32_Bit_q31[2]), .d30(undriven_6), .q30(Instruction_Format__32_Bit_q31[1]),
    .d31(undriven_7), .q31(Instruction_Format__32_Bit_q31[0]));  // open: shift, out, clr, d0, d1, d2, d6, d7, d10, d11, d14, d15, d16, d17, d18, d19, d20, d21, d22, d23, d24, d25, d26, d27, d28, d29
  assign ram_2_data = Store ? B : 32'bz;  // Controlled_Buffer controlled_buffer_1
  RAM #(.addrWidth(16), .dataWidth(32)) ram_3 (.addr(Program_Counter_q), .data(ram_3_data));  // open: sel, clk, ld, clr
  // Probe on Instruction_Format__32_Bit_q31
  or or_1 (or_1_out, LoadL, Load);
  Register #(.width(32)) Instruction_Register (
    .D(ram_3_data), .en(in_10),
    .Q({Instruction_Register_q[31:27], Addr[7:5], {2{Addr[5]}}, {3{Addr[2]}}, Instruction_Register_q[18:11], Addr[7:6], Addr[6:5], {2{Addr[5]}}, {3{Addr[2]}}, Instruction_Register_q[1:0]}),
    .clk(clock_4_out));  // open: clr
  Clock clock_4 (.out(clock_4_out));
  or or_2 (Write, LoadL, Load, Data);
  Controlled_Buffer #(.width(32)) controlled_buffer_2 (.out(in_val), .en(Data));  // open: in
  assign in_val = Load ? ram_2_data : 32'bz;  // Controlled_Buffer controlled_buffer_3
  assign bit_extender_4_out = {{30{1'b0}}, {2{Addr[2]}}};  // Bit_Extender bit_extender_4
  assign in_val = LoadL ? bit_extender_4_out : 32'bz;  // Controlled_Buffer controlled_buffer_4
  assign Rd = or_1_out ? Rb : 4'bz;  // Controlled_Buffer controlled_buffer_5
  assign bit_extender_5_out = {{2{1'b0}}, {2{Addr[5]}}};  // Bit_Extender bit_extender_5
  assign Rd = Data ? bit_extender_5_out : 4'bz;  // Controlled_Buffer controlled_buffer_6
  Clock clk (.out(clk_out));
  Demultiplexer #(.select(4)) demultiplexer_1 (
    .out0(demultiplexer_1_out0), .out1(demultiplexer_1_out1), .out2(demultiplexer_1_out2),
    .out3(demultiplexer_1_out3), .out4(demultiplexer_1_out4), .out5(demultiplexer_1_out5),
    .out6(demultiplexer_1_out6), .out7(demultiplexer_1_out7), .out8(demultiplexer_1_out8),
    .out9(demultiplexer_1_out9), .out10(demultiplexer_1_out10), .out11(demultiplexer_1_out11),
    .out12(demultiplexer_1_out12), .out13(demultiplexer_1_out13), .out14(demultiplexer_1_out14),
    .out15(demultiplexer_1_out15), .in(Write), .sel(Rd));  // open: en
  assign Ra = {{2{1'b0}}, {2{Addr[2]}}};  // Bit_Extender bit_extender_6
  assign Rb = {{2{1'b0}}, Instruction_Register_q[17:16]};  // Bit_Extender bit_extender_7
  assign Ra = {{2{1'b0}}, {2{Addr[2]}}};  // Bit_Extender bit_extender_8
  assign Rb = {{2{1'b0}}, Instruction_Register_q[1:0]};  // Bit_Extender bit_extender_9
  Register #(.width(32)) R0 (.D(in_val), .en(demultiplexer_1_out0), .Q(R0_q), .clk(clk_out));  // open: clr
  Register #(.width(32)) R1 (.D(in_val), .en(demultiplexer_1_out1), .Q(R1_q), .clk(clk_out));  // open: clr
  Register #(.width(32)) R2 (.D(in_val), .en(demultiplexer_1_out2), .Q(R2_q), .clk(clk_out));  // open: clr
  Register #(.width(32)) R3 (.D(in_val), .en(demultiplexer_1_out3), .Q(R3_q), .clk(clk_out));  // open: clr
  Register #(.width(32)) R4 (.D(in_val), .en(demultiplexer_1_out4), .Q(R4_q), .clk(clk_out));  // open: clr
  Register #(.width(32)) R5 (.D(in_val), .en(demultiplexer_1_out5), .Q(R5_q), .clk(clk_out));  // open: clr
  Register #(.width(32)) R6 (.D(in_val), .en(demultiplexer_1_out6), .Q(R6_q), .clk(clk_out));  // open: clr
  Register #(.width(32)) R7 (.D(in_val), .en(demultiplexer_1_out7), .Q(R7_q), .clk(clk_out));  // open: clr
  Register #(.width(32)) R8 (.D(in_val), .en(demultiplexer_1_out8), .Q(R8_q), .clk(clk_out));  // open: clr
  Register #(.width(32)) R9 (.D(in_val), .en(demultiplexer_1_out9), .Q(R9_q), .clk(clk_out));  // open: clr
  Register #(.width(32)) R10 (.D(in_val), .en(demultiplexer_1_out10), .Q(R10_q), .clk(clk_out));  // open: clr
  Register #(.width(32)) R11 (.D(in_val), .en(demultiplexer_1_out11), .Q(R11_q), .clk(clk_out));  // open: clr
  Register #(.width(32)) R12 (.D(in_val), .en(demultiplexer_1_out12), .Q(R12_q), .clk(clk_out));  // open: clr
  Register #(.width(32)) R13 (.D(in_val), .en(demultiplexer_1_out13), .Q(R13_q), .clk(clk_out));  // open: clr
  Register #(.width(32)) R14 (.D(in_val), .en(demultiplexer_1_out14), .Q(R14_q), .clk(clk_out));  // open: clr
  Register #(.width(32)) R15 (.D(in_val), .en(demultiplexer_1_out15), .Q(R15_q), .clk(clk_out));  // open: clr
  and and_1 (Data, ~Instruction_Register_q[15], ~Instruction_Register_q[14], Instruction_Register_q[13]);  // AND_Gate
  and and_2 (Load, ~Instruction_Register_q[15], Instruction_Register_q[14], ~Instruction_Register_q[13]);  // AND_Gate
  and and_3 (Store, Instruction_Register_q[15], ~Instruction_Register_q[14], ~Instruction_Register_q[13]);  // AND_Gate
  and and_4 (LoadL, ~Instruction_Register_q[15], Instruction_Register_q[14], Instruction_Register_q[13]);  // AND_Gate
  and and_5 (Data, ~Instruction_Register_q[31], ~Instruction_Register_q[30], Instruction_Register_q[29]);  // AND_Gate
  and and_6 (Load, ~Instruction_Register_q[31], Instruction_Register_q[30], ~Instruction_Register_q[29]);  // AND_Gate
  and and_7 (Store, Instruction_Register_q[31], ~Instruction_Register_q[30], ~Instruction_Register_q[29]);  // AND_Gate
  and and_8 (LoadL, ~Instruction_Register_q[31], Instruction_Register_q[30], Instruction_Register_q[29]);  // AND_Gate
  Multiplexer #(.select(4), .width(32)) multiplexer_2 (
    .in0(R0_q), .in1(R1_q), .in2(R2_q), .in3(R3_q), .in4(R4_q), .in5(R5_q), .in6(R6_q), .in7(R7_q),
    .in8(R8_q), .in9(R9_q), .in10(R10_q), .in11(R11_q), .in12(R12_q), .in13(R13_q), .in14(R14_q),
    .in15(R15_q), .out(A), .sel(Ra));  // open: en
  Multiplexer #(.select(4), .width(32)) multiplexer_3 (
    .in0(R0_q), .in1(R1_q), .in2(R2_q), .in3(R3_q), .in4(R4_q), .in5(R5_q), .in6(R6_q), .in7(R7_q),
    .in8(R8_q), .in9(R9_q), .in10(R10_q), .in11(R11_q), .in12(R12_q), .in13(R13_q), .in14(R14_q),
    .in15(R15_q), .out(B), .sel(Rb));  // open: en
  _1b_ALU u_1b_alu_1 (
    .A(A[0]), .B(B[0]), .Less(n1b_alu_32_out_9), .Result(R[0]), .Sub(Sub), .Cin(Sub), .in_3(Op),
    .Cout(n1b_alu_1_cout));  // open: out_9
  _1b_ALU u_1b_alu_2 (
    .A(A[1]), .B(B[1]), .Less(1'b0), .Result(R[1]), .Sub(Sub), .Cin(n1b_alu_1_cout), .in_3(Op),
    .Cout(n1b_alu_2_cout));  // open: out_9
  _1b_ALU u_1b_alu_3 (
    .A(A[2]), .B(B[2]), .Less(1'b0), .Result(R[2]), .Sub(Sub), .Cin(n1b_alu_2_cout), .in_3(Op),
    .Cout(n1b_alu_3_cout));  // open: out_9
  _1b_ALU u_1b_alu_4 (
    .A(A[3]), .B(B[3]), .Less(1'b0), .Result(R[3]), .Sub(Sub), .Cin(n1b_alu_3_cout), .in_3(Op),
    .Cout(n1b_alu_4_cout));  // open: out_9
  _1b_ALU u_1b_alu_5 (
    .A(A[4]), .B(B[4]), .Less(1'b0), .Result(R[4]), .Sub(Sub), .Cin(n1b_alu_4_cout), .in_3(Op),
    .Cout(n1b_alu_5_cout));  // open: out_9
  _1b_ALU u_1b_alu_6 (
    .A(A[5]), .B(B[5]), .Less(1'b0), .Result(R[5]), .Sub(Sub), .Cin(n1b_alu_5_cout), .in_3(Op),
    .Cout(n1b_alu_6_cout));  // open: out_9
  _1b_ALU u_1b_alu_7 (
    .A(A[6]), .B(B[6]), .Less(1'b0), .Result(R[6]), .Sub(Sub), .Cin(n1b_alu_6_cout), .in_3(Op),
    .Cout(n1b_alu_7_cout));  // open: out_9
  _1b_ALU u_1b_alu_8 (
    .A(A[7]), .B(B[7]), .Less(1'b0), .Result(R[7]), .Sub(Sub), .Cin(n1b_alu_7_cout), .in_3(Op),
    .Cout(n1b_alu_8_cout));  // open: out_9
  _1b_ALU u_1b_alu_9 (
    .A(A[8]), .B(B[8]), .Less(1'b0), .Result(R[8]), .Sub(Sub), .Cin(n1b_alu_8_cout), .in_3(Op),
    .Cout(n1b_alu_9_cout));  // open: out_9
  _1b_ALU u_1b_alu_10 (
    .A(A[9]), .B(B[9]), .Less(1'b0), .Result(R[9]), .Sub(Sub), .Cin(n1b_alu_9_cout), .in_3(Op),
    .Cout(n1b_alu_10_cout));  // open: out_9
  _1b_ALU u_1b_alu_11 (
    .A(A[10]), .B(B[10]), .Less(1'b0), .Result(R[10]), .Sub(Sub), .Cin(n1b_alu_10_cout), .in_3(Op),
    .Cout(n1b_alu_11_cout));  // open: out_9
  _1b_ALU u_1b_alu_12 (
    .A(A[11]), .B(B[11]), .Less(1'b0), .Result(R[11]), .Sub(Sub), .Cin(n1b_alu_11_cout), .in_3(Op),
    .Cout(n1b_alu_12_cout));  // open: out_9
  _1b_ALU u_1b_alu_13 (
    .A(A[12]), .B(B[12]), .Less(1'b0), .Result(R[12]), .Sub(Sub), .Cin(n1b_alu_12_cout), .in_3(Op),
    .Cout(n1b_alu_13_cout));  // open: out_9
  _1b_ALU u_1b_alu_14 (
    .A(A[13]), .B(B[13]), .Less(1'b0), .Result(R[13]), .Sub(Sub), .Cin(n1b_alu_13_cout), .in_3(Op),
    .Cout(n1b_alu_14_cout));  // open: out_9
  _1b_ALU u_1b_alu_15 (
    .A(A[14]), .B(B[14]), .Less(1'b0), .Result(R[14]), .Sub(Sub), .Cin(n1b_alu_14_cout), .in_3(Op),
    .Cout(n1b_alu_15_cout));  // open: out_9
  _1b_ALU u_1b_alu_16 (
    .A(A[15]), .B(B[15]), .Less(1'b0), .Result(R[15]), .Sub(Sub), .Cin(n1b_alu_15_cout), .in_3(Op),
    .Cout(n1b_alu_16_cout));  // open: out_9
  _1b_ALU u_1b_alu_17 (
    .A(A[16]), .B(B[16]), .Less(1'b0), .Result(R[16]), .Sub(Sub), .Cin(n1b_alu_16_cout), .in_3(Op),
    .Cout(n1b_alu_17_cout));  // open: out_9
  _1b_ALU u_1b_alu_18 (
    .A(A[17]), .B(B[17]), .Less(1'b0), .Result(R[17]), .Sub(Sub), .Cin(n1b_alu_17_cout), .in_3(Op),
    .Cout(n1b_alu_18_cout));  // open: out_9
  _1b_ALU u_1b_alu_19 (
    .A(A[18]), .B(B[18]), .Less(1'b0), .Result(R[18]), .Sub(Sub), .Cin(n1b_alu_18_cout), .in_3(Op),
    .Cout(n1b_alu_19_cout));  // open: out_9
  _1b_ALU u_1b_alu_20 (
    .A(A[19]), .B(B[19]), .Less(1'b0), .Result(R[19]), .Sub(Sub), .Cin(n1b_alu_19_cout), .in_3(Op),
    .Cout(n1b_alu_20_cout));  // open: out_9
  _1b_ALU u_1b_alu_21 (
    .A(A[20]), .B(B[20]), .Less(1'b0), .Result(R[20]), .Sub(Sub), .Cin(n1b_alu_20_cout), .in_3(Op),
    .Cout(n1b_alu_21_cout));  // open: out_9
  _1b_ALU u_1b_alu_22 (
    .A(A[21]), .B(B[21]), .Less(1'b0), .Result(R[21]), .Sub(Sub), .Cin(n1b_alu_21_cout), .in_3(Op),
    .Cout(n1b_alu_22_cout));  // open: out_9
  _1b_ALU u_1b_alu_23 (
    .A(A[22]), .B(B[22]), .Less(1'b0), .Result(R[22]), .Sub(Sub), .Cin(n1b_alu_22_cout), .in_3(Op),
    .Cout(n1b_alu_23_cout));  // open: out_9
  _1b_ALU u_1b_alu_24 (
    .A(A[23]), .B(B[23]), .Less(1'b0), .Result(R[23]), .Sub(Sub), .Cin(n1b_alu_23_cout), .in_3(Op),
    .Cout(n1b_alu_24_cout));  // open: out_9
  _1b_ALU u_1b_alu_25 (
    .A(A[24]), .B(B[24]), .Less(1'b0), .Result(R[24]), .Sub(Sub), .Cin(n1b_alu_24_cout), .in_3(Op),
    .Cout(n1b_alu_25_cout));  // open: out_9
  _1b_ALU u_1b_alu_26 (
    .A(A[25]), .B(B[25]), .Less(1'b0), .Result(R[25]), .Sub(Sub), .Cin(n1b_alu_25_cout), .in_3(Op),
    .Cout(n1b_alu_26_cout));  // open: out_9
  _1b_ALU u_1b_alu_27 (
    .A(A[26]), .B(B[26]), .Less(1'b0), .Result(R[26]), .Sub(Sub), .Cin(n1b_alu_26_cout), .in_3(Op),
    .Cout(n1b_alu_27_cout));  // open: out_9
  _1b_ALU u_1b_alu_28 (
    .A(A[27]), .B(B[27]), .Less(1'b0), .Result(R[27]), .Sub(Sub), .Cin(n1b_alu_27_cout), .in_3(Op),
    .Cout(n1b_alu_28_cout));  // open: out_9
  _1b_ALU u_1b_alu_29 (
    .A(A[28]), .B(B[28]), .Less(1'b0), .Result(R[28]), .Sub(Sub), .Cin(n1b_alu_28_cout), .in_3(Op),
    .Cout(n1b_alu_29_cout));  // open: out_9
  _1b_ALU u_1b_alu_30 (
    .A(A[29]), .B(B[29]), .Less(1'b0), .Result(R[29]), .Sub(Sub), .Cin(n1b_alu_29_cout), .in_3(Op),
    .Cout(n1b_alu_30_cout));  // open: out_9
  _1b_ALU u_1b_alu_31 (
    .A(A[30]), .B(B[30]), .Less(1'b0), .Result(R[30]), .Sub(Sub), .Cin(n1b_alu_30_cout), .in_3(Op),
    .Cout(n1b_alu_31_cout));  // open: out_9
  _1b_ALU u_1b_alu_32 (
    .A(A[31]), .B(B[31]), .Less(1'b0), .Result(R[31]), .out_9(n1b_alu_32_out_9), .Sub(Sub),
    .Cin(n1b_alu_31_cout), .in_3(Op));  // open: Cout
  nor nor_1 (Zero, R[0], R[1], R[2], R[3], R[4], R[5], R[6], R[7], R[8], R[9], R[10], R[11], R[12], R[13], R[14], R[15], R[16], R[17], R[18], R[19], R[20], R[21], R[22], R[23], R[24], R[25], R[26], R[27], R[28], R[29], R[30], R[31]);

  assign out_a = A;
  assign out_b = B;

  // Other names for the same wires on the sheet: Addr (some bits) = {{2{Addr[5]}}, {2{Addr[2]}}};
  //   Value[1:0] = {2{Addr[2]}}; Rd_t[1:0] = {2{Addr[5]}}; op_t[1:0] = Addr[7:6]; memEn = Zero

  // Notes on the sheet:
  //   Memory Unit
  //   Mem Data, Hex
  //   Data Memory
  //   I
  //   opcode
  //   rd
  //   Instruction Memory
  //   rs1
  //   Immediate
  //   Calculate Immediate
  //   Control Buffers
  //   en Im
  //   Instruction Decoder
  //   Control Unit
  //   Register Files (Register Bank)
  //   ALU
endmodule

module _1b_ALU (
  input  Sub,
  input  Cin,
  input  [2:0] in_3,
  input  A,
  input  B,
  input  Less,
  output Result,
  output Cout,
  output out_9
);

  wire adder_1_out, and_1_out, nor_1_out, xor_1_out, xor_2_out;

  xor xor_1 (xor_1_out, B, Sub);
  and and_1 (and_1_out, A, B);
  or or_1 (and_1_out, A, B);
  xor xor_2 (xor_2_out, A, B);
  nor nor_1 (nor_1_out, A, B);
  Adder #(.width(1)) adder_1 (.a(A), .b(xor_1_out), .out(adder_1_out), .cin(Cin), .cout(Cout));
  Multiplexer #(.select(3), .enable("false")) multiplexer_1 (
    .in0(and_1_out), .in1(and_1_out), .in2(xor_2_out), .in3(nor_1_out), .in4(adder_1_out), .in5(Less),
    .out(Result), .sel(in_3));  // open: in6, in7

  // Notes on the sheet:
  //   ALU Operations
  //   AND
  //   OR
  //   XOR
  //   NOR
  //   ADD/SUB
endmodule

module ALU (
  input  Sub,
  input  [2:0] Op,
  input  [31:0] A,
  input  [31:0] B,
  output [31:0] R,
  output Zero
);

  wire n1b_alu_1_cout, n1b_alu_2_cout, n1b_alu_3_cout, n1b_alu_4_cout, n1b_alu_5_cout, n1b_alu_6_cout,
       n1b_alu_7_cout, n1b_alu_8_cout, n1b_alu_9_cout, n1b_alu_10_cout, n1b_alu_11_cout, n1b_alu_12_cout,
       n1b_alu_13_cout, n1b_alu_14_cout, n1b_alu_15_cout, n1b_alu_16_cout, n1b_alu_17_cout, n1b_alu_18_cout,
       n1b_alu_19_cout, n1b_alu_20_cout, n1b_alu_21_cout, n1b_alu_22_cout, n1b_alu_23_cout, n1b_alu_24_cout,
       n1b_alu_25_cout, n1b_alu_26_cout, n1b_alu_27_cout, n1b_alu_28_cout, n1b_alu_29_cout, n1b_alu_30_cout,
       n1b_alu_31_cout, n1b_alu_32_out_9;

  _1b_ALU u_1b_alu_1 (
    .A(A[0]), .B(B[0]), .Less(n1b_alu_32_out_9), .Result(R[0]), .Sub(Sub), .Cin(Sub), .in_3(Op),
    .Cout(n1b_alu_1_cout));  // open: out_9
  _1b_ALU u_1b_alu_2 (
    .A(A[1]), .B(B[1]), .Less(1'b0), .Result(R[1]), .Sub(Sub), .Cin(n1b_alu_1_cout), .in_3(Op),
    .Cout(n1b_alu_2_cout));  // open: out_9
  _1b_ALU u_1b_alu_3 (
    .A(A[2]), .B(B[2]), .Less(1'b0), .Result(R[2]), .Sub(Sub), .Cin(n1b_alu_2_cout), .in_3(Op),
    .Cout(n1b_alu_3_cout));  // open: out_9
  _1b_ALU u_1b_alu_4 (
    .A(A[3]), .B(B[3]), .Less(1'b0), .Result(R[3]), .Sub(Sub), .Cin(n1b_alu_3_cout), .in_3(Op),
    .Cout(n1b_alu_4_cout));  // open: out_9
  _1b_ALU u_1b_alu_5 (
    .A(A[4]), .B(B[4]), .Less(1'b0), .Result(R[4]), .Sub(Sub), .Cin(n1b_alu_4_cout), .in_3(Op),
    .Cout(n1b_alu_5_cout));  // open: out_9
  _1b_ALU u_1b_alu_6 (
    .A(A[5]), .B(B[5]), .Less(1'b0), .Result(R[5]), .Sub(Sub), .Cin(n1b_alu_5_cout), .in_3(Op),
    .Cout(n1b_alu_6_cout));  // open: out_9
  _1b_ALU u_1b_alu_7 (
    .A(A[6]), .B(B[6]), .Less(1'b0), .Result(R[6]), .Sub(Sub), .Cin(n1b_alu_6_cout), .in_3(Op),
    .Cout(n1b_alu_7_cout));  // open: out_9
  _1b_ALU u_1b_alu_8 (
    .A(A[7]), .B(B[7]), .Less(1'b0), .Result(R[7]), .Sub(Sub), .Cin(n1b_alu_7_cout), .in_3(Op),
    .Cout(n1b_alu_8_cout));  // open: out_9
  _1b_ALU u_1b_alu_9 (
    .A(A[8]), .B(B[8]), .Less(1'b0), .Result(R[8]), .Sub(Sub), .Cin(n1b_alu_8_cout), .in_3(Op),
    .Cout(n1b_alu_9_cout));  // open: out_9
  _1b_ALU u_1b_alu_10 (
    .A(A[9]), .B(B[9]), .Less(1'b0), .Result(R[9]), .Sub(Sub), .Cin(n1b_alu_9_cout), .in_3(Op),
    .Cout(n1b_alu_10_cout));  // open: out_9
  _1b_ALU u_1b_alu_11 (
    .A(A[10]), .B(B[10]), .Less(1'b0), .Result(R[10]), .Sub(Sub), .Cin(n1b_alu_10_cout), .in_3(Op),
    .Cout(n1b_alu_11_cout));  // open: out_9
  _1b_ALU u_1b_alu_12 (
    .A(A[11]), .B(B[11]), .Less(1'b0), .Result(R[11]), .Sub(Sub), .Cin(n1b_alu_11_cout), .in_3(Op),
    .Cout(n1b_alu_12_cout));  // open: out_9
  _1b_ALU u_1b_alu_13 (
    .A(A[12]), .B(B[12]), .Less(1'b0), .Result(R[12]), .Sub(Sub), .Cin(n1b_alu_12_cout), .in_3(Op),
    .Cout(n1b_alu_13_cout));  // open: out_9
  _1b_ALU u_1b_alu_14 (
    .A(A[13]), .B(B[13]), .Less(1'b0), .Result(R[13]), .Sub(Sub), .Cin(n1b_alu_13_cout), .in_3(Op),
    .Cout(n1b_alu_14_cout));  // open: out_9
  _1b_ALU u_1b_alu_15 (
    .A(A[14]), .B(B[14]), .Less(1'b0), .Result(R[14]), .Sub(Sub), .Cin(n1b_alu_14_cout), .in_3(Op),
    .Cout(n1b_alu_15_cout));  // open: out_9
  _1b_ALU u_1b_alu_16 (
    .A(A[15]), .B(B[15]), .Less(1'b0), .Result(R[15]), .Sub(Sub), .Cin(n1b_alu_15_cout), .in_3(Op),
    .Cout(n1b_alu_16_cout));  // open: out_9
  _1b_ALU u_1b_alu_17 (
    .A(A[16]), .B(B[16]), .Less(1'b0), .Result(R[16]), .Sub(Sub), .Cin(n1b_alu_16_cout), .in_3(Op),
    .Cout(n1b_alu_17_cout));  // open: out_9
  _1b_ALU u_1b_alu_18 (
    .A(A[17]), .B(B[17]), .Less(1'b0), .Result(R[17]), .Sub(Sub), .Cin(n1b_alu_17_cout), .in_3(Op),
    .Cout(n1b_alu_18_cout));  // open: out_9
  _1b_ALU u_1b_alu_19 (
    .A(A[18]), .B(B[18]), .Less(1'b0), .Result(R[18]), .Sub(Sub), .Cin(n1b_alu_18_cout), .in_3(Op),
    .Cout(n1b_alu_19_cout));  // open: out_9
  _1b_ALU u_1b_alu_20 (
    .A(A[19]), .B(B[19]), .Less(1'b0), .Result(R[19]), .Sub(Sub), .Cin(n1b_alu_19_cout), .in_3(Op),
    .Cout(n1b_alu_20_cout));  // open: out_9
  _1b_ALU u_1b_alu_21 (
    .A(A[20]), .B(B[20]), .Less(1'b0), .Result(R[20]), .Sub(Sub), .Cin(n1b_alu_20_cout), .in_3(Op),
    .Cout(n1b_alu_21_cout));  // open: out_9
  _1b_ALU u_1b_alu_22 (
    .A(A[21]), .B(B[21]), .Less(1'b0), .Result(R[21]), .Sub(Sub), .Cin(n1b_alu_21_cout), .in_3(Op),
    .Cout(n1b_alu_22_cout));  // open: out_9
  _1b_ALU u_1b_alu_23 (
    .A(A[22]), .B(B[22]), .Less(1'b0), .Result(R[22]), .Sub(Sub), .Cin(n1b_alu_22_cout), .in_3(Op),
    .Cout(n1b_alu_23_cout));  // open: out_9
  _1b_ALU u_1b_alu_24 (
    .A(A[23]), .B(B[23]), .Less(1'b0), .Result(R[23]), .Sub(Sub), .Cin(n1b_alu_23_cout), .in_3(Op),
    .Cout(n1b_alu_24_cout));  // open: out_9
  _1b_ALU u_1b_alu_25 (
    .A(A[24]), .B(B[24]), .Less(1'b0), .Result(R[24]), .Sub(Sub), .Cin(n1b_alu_24_cout), .in_3(Op),
    .Cout(n1b_alu_25_cout));  // open: out_9
  _1b_ALU u_1b_alu_26 (
    .A(A[25]), .B(B[25]), .Less(1'b0), .Result(R[25]), .Sub(Sub), .Cin(n1b_alu_25_cout), .in_3(Op),
    .Cout(n1b_alu_26_cout));  // open: out_9
  _1b_ALU u_1b_alu_27 (
    .A(A[26]), .B(B[26]), .Less(1'b0), .Result(R[26]), .Sub(Sub), .Cin(n1b_alu_26_cout), .in_3(Op),
    .Cout(n1b_alu_27_cout));  // open: out_9
  _1b_ALU u_1b_alu_28 (
    .A(A[27]), .B(B[27]), .Less(1'b0), .Result(R[27]), .Sub(Sub), .Cin(n1b_alu_27_cout), .in_3(Op),
    .Cout(n1b_alu_28_cout));  // open: out_9
  _1b_ALU u_1b_alu_29 (
    .A(A[28]), .B(B[28]), .Less(1'b0), .Result(R[28]), .Sub(Sub), .Cin(n1b_alu_28_cout), .in_3(Op),
    .Cout(n1b_alu_29_cout));  // open: out_9
  _1b_ALU u_1b_alu_30 (
    .A(A[29]), .B(B[29]), .Less(1'b0), .Result(R[29]), .Sub(Sub), .Cin(n1b_alu_29_cout), .in_3(Op),
    .Cout(n1b_alu_30_cout));  // open: out_9
  _1b_ALU u_1b_alu_31 (
    .A(A[30]), .B(B[30]), .Less(1'b0), .Result(R[30]), .Sub(Sub), .Cin(n1b_alu_30_cout), .in_3(Op),
    .Cout(n1b_alu_31_cout));  // open: out_9
  _1b_ALU u_1b_alu_32 (
    .A(A[31]), .B(B[31]), .Less(1'b0), .Result(R[31]), .out_9(n1b_alu_32_out_9), .Sub(Sub),
    .Cin(n1b_alu_31_cout), .in_3(Op));  // open: Cout
  nor nor_1 (Zero, R[0], R[1], R[2], R[3], R[4], R[5], R[6], R[7], R[8], R[9], R[10], R[11], R[12], R[13], R[14], R[15], R[16], R[17], R[18], R[19], R[20], R[21], R[22], R[23], R[24], R[25], R[26], R[27], R[28], R[29], R[30], R[31]);

  // Notes on the sheet:
  //   ALU
endmodule

module Register_Bank (
  input  Write,
  input  [31:0] in_val,
  input  [3:0] Rd,
  input  [3:0] Ra,
  input  [3:0] Rb,
  output [31:0] out_a,
  output [31:0] out_b
);

  wire clk_out, demultiplexer_1_out0, demultiplexer_1_out1, demultiplexer_1_out2, demultiplexer_1_out3,
       demultiplexer_1_out4, demultiplexer_1_out5, demultiplexer_1_out6, demultiplexer_1_out7,
       demultiplexer_1_out8, demultiplexer_1_out9, demultiplexer_1_out10, demultiplexer_1_out11,
       demultiplexer_1_out12, demultiplexer_1_out13, demultiplexer_1_out14, demultiplexer_1_out15;
  wire [31:0] R0_q, R1_q, R2_q, R3_q, R4_q, R5_q, R6_q, R7_q, R8_q, R9_q, R10_q, R11_q, R12_q, R13_q, R14_q,
       R15_q;

  Clock clk (.out(clk_out));
  Demultiplexer #(.select(4)) demultiplexer_1 (
    .out0(demultiplexer_1_out0), .out1(demultiplexer_1_out1), .out2(demultiplexer_1_out2),
    .out3(demultiplexer_1_out3), .out4(demultiplexer_1_out4), .out5(demultiplexer_1_out5),
    .out6(demultiplexer_1_out6), .out7(demultiplexer_1_out7), .out8(demultiplexer_1_out8),
    .out9(demultiplexer_1_out9), .out10(demultiplexer_1_out10), .out11(demultiplexer_1_out11),
    .out12(demultiplexer_1_out12), .out13(demultiplexer_1_out13), .out14(demultiplexer_1_out14),
    .out15(demultiplexer_1_out15), .in(Write), .sel(Rd));  // open: en
  Register #(.width(32)) R0 (.D(in_val), .en(demultiplexer_1_out0), .Q(R0_q), .clk(clk_out));  // open: clr
  Register #(.width(32)) R1 (.D(in_val), .en(demultiplexer_1_out1), .Q(R1_q), .clk(clk_out));  // open: clr
  Register #(.width(32)) R2 (.D(in_val), .en(demultiplexer_1_out2), .Q(R2_q), .clk(clk_out));  // open: clr
  Register #(.width(32)) R3 (.D(in_val), .en(demultiplexer_1_out3), .Q(R3_q), .clk(clk_out));  // open: clr
  Register #(.width(32)) R4 (.D(in_val), .en(demultiplexer_1_out4), .Q(R4_q), .clk(clk_out));  // open: clr
  Register #(.width(32)) R5 (.D(in_val), .en(demultiplexer_1_out5), .Q(R5_q), .clk(clk_out));  // open: clr
  Register #(.width(32)) R6 (.D(in_val), .en(demultiplexer_1_out6), .Q(R6_q), .clk(clk_out));  // open: clr
  Register #(.width(32)) R7 (.D(in_val), .en(demultiplexer_1_out7), .Q(R7_q), .clk(clk_out));  // open: clr
  Register #(.width(32)) R8 (.D(in_val), .en(demultiplexer_1_out8), .Q(R8_q), .clk(clk_out));  // open: clr
  Register #(.width(32)) R9 (.D(in_val), .en(demultiplexer_1_out9), .Q(R9_q), .clk(clk_out));  // open: clr
  Register #(.width(32)) R10 (.D(in_val), .en(demultiplexer_1_out10), .Q(R10_q), .clk(clk_out));  // open: clr
  Register #(.width(32)) R11 (.D(in_val), .en(demultiplexer_1_out11), .Q(R11_q), .clk(clk_out));  // open: clr
  Register #(.width(32)) R12 (.D(in_val), .en(demultiplexer_1_out12), .Q(R12_q), .clk(clk_out));  // open: clr
  Register #(.width(32)) R13 (.D(in_val), .en(demultiplexer_1_out13), .Q(R13_q), .clk(clk_out));  // open: clr
  Register #(.width(32)) R14 (.D(in_val), .en(demultiplexer_1_out14), .Q(R14_q), .clk(clk_out));  // open: clr
  Register #(.width(32)) R15 (.D(in_val), .en(demultiplexer_1_out15), .Q(R15_q), .clk(clk_out));  // open: clr
  Multiplexer #(.select(4), .width(32)) multiplexer_1 (
    .in0(R0_q), .in1(R1_q), .in2(R2_q), .in3(R3_q), .in4(R4_q), .in5(R5_q), .in6(R6_q), .in7(R7_q),
    .in8(R8_q), .in9(R9_q), .in10(R10_q), .in11(R11_q), .in12(R12_q), .in13(R13_q), .in14(R14_q),
    .in15(R15_q), .out(out_a), .sel(Ra));  // open: en
  Multiplexer #(.select(4), .width(32)) multiplexer_2 (
    .in0(R0_q), .in1(R1_q), .in2(R2_q), .in3(R3_q), .in4(R4_q), .in5(R5_q), .in6(R6_q), .in7(R7_q),
    .in8(R8_q), .in9(R9_q), .in10(R10_q), .in11(R11_q), .in12(R12_q), .in13(R13_q), .in14(R14_q),
    .in15(R15_q), .out(out_b), .sel(Rb));  // open: en

  // Notes on the sheet:
  //   Register Files (Register Bank)
endmodule

module Instruction_Memory (
);

  wire clock_1_out;
  wire [15:0] Program_Counter_q;

  Counter #(.width(16), .max('hffff)) Program_Counter (
    .Q(Program_Counter_q), .clk(clock_1_out));  // open: load, D, count, carry, clr
  Clock clock_1 (.out(clock_1_out));
  RAM #(.addrWidth(16), .dataWidth(32)) ram_1 (.addr(Program_Counter_q));  // open: data, sel, clk, ld, clr

  // Notes on the sheet:
  //   Instruction Memory
endmodule

module Control_Unit (
  input  in_1
);

  wire clock_1_out, Data, Load, LoadL, Store, undriven, undriven_2, undriven_3, undriven_4, undriven_5,
       undriven_6;
  wire [1:0] Rb, Rd;
  wire [1:1] Addr;
  wire [5:5] Instruction_Register_q;

  Register Instruction_Register (
    .en(in_1), .Q({Rd, Instruction_Register_q[5], {3{Addr[1]}}, Rb}), .clk(clock_1_out));  // open: D, clr
  Clock clock_1 (.out(clock_1_out));
  and and_1 (Data, ~undriven_4, ~undriven_5, undriven_6);  // AND_Gate
  and and_2 (Load, ~undriven_4, undriven_5, ~undriven_6);  // AND_Gate
  and and_3 (Store, undriven_4, ~undriven_5, ~undriven_6);  // AND_Gate
  and and_4 (LoadL, ~undriven_4, undriven_5, undriven_6);  // AND_Gate
  and and_5 (Data, ~undriven, ~undriven_2, undriven_3);  // AND_Gate
  and and_6 (Load, ~undriven, undriven_2, ~undriven_3);  // AND_Gate
  and and_7 (Store, undriven, ~undriven_2, ~undriven_3);  // AND_Gate
  and and_8 (LoadL, ~undriven, undriven_2, undriven_3);  // AND_Gate

  // Other names for the same wires on the sheet: Addr[0] = Addr[1]; Ra[1:0] = {2{Addr[1]}}; Value[1:0] = {2{Addr[1]}}

  // Notes on the sheet:
  //   Instruction Decoder
  //   Control Unit
endmodule

module Calculate_Immediate (
);

  wire undriven, undriven_2, undriven_3, undriven_4, undriven_5, undriven_6;
  wire [31:0] Instruction_Format__32_Bit_q31;

  Shift_Register #(.length(32)) Instruction_Format__32_Bit (
    .in(1'b1), .clk(1'b1), .load(undriven), .q0(Instruction_Format__32_Bit_q31[31]),
    .q1(Instruction_Format__32_Bit_q31[30]), .q2(Instruction_Format__32_Bit_q31[29]), .d3(undriven),
    .q3(Instruction_Format__32_Bit_q31[28]), .d4(undriven_2), .q4(Instruction_Format__32_Bit_q31[27]),
    .d5(undriven_3), .q5(Instruction_Format__32_Bit_q31[26]), .q6(Instruction_Format__32_Bit_q31[25]),
    .q7(Instruction_Format__32_Bit_q31[24]), .d8(undriven_3), .q8(Instruction_Format__32_Bit_q31[23]),
    .d9(undriven_4), .q9(Instruction_Format__32_Bit_q31[22]), .q10(Instruction_Format__32_Bit_q31[21]),
    .q11(Instruction_Format__32_Bit_q31[20]), .d12(undriven_4), .q12(Instruction_Format__32_Bit_q31[19]),
    .d13(undriven_5), .q13(Instruction_Format__32_Bit_q31[18]), .q14(Instruction_Format__32_Bit_q31[17]),
    .q15(Instruction_Format__32_Bit_q31[16]), .q16(Instruction_Format__32_Bit_q31[15]),
    .q17(Instruction_Format__32_Bit_q31[14]), .q18(Instruction_Format__32_Bit_q31[13]),
    .q19(Instruction_Format__32_Bit_q31[12]), .q20(Instruction_Format__32_Bit_q31[11]),
    .q21(Instruction_Format__32_Bit_q31[10]), .q22(Instruction_Format__32_Bit_q31[9]),
    .q23(Instruction_Format__32_Bit_q31[8]), .q24(Instruction_Format__32_Bit_q31[7]),
    .q25(Instruction_Format__32_Bit_q31[6]), .q26(Instruction_Format__32_Bit_q31[5]),
    .q27(Instruction_Format__32_Bit_q31[4]), .q28(Instruction_Format__32_Bit_q31[3]),
    .q29(Instruction_Format__32_Bit_q31[2]), .d30(undriven_5), .q30(Instruction_Format__32_Bit_q31[1]),
    .d31(undriven_6), .q31(Instruction_Format__32_Bit_q31[0]));  // open: shift, out, clr, d0, d1, d2, d6, d7, d10, d11, d14, d15, d16, d17, d18, d19, d20, d21, d22, d23, d24, d25, d26, d27, d28, d29
  // Probe on Instruction_Format__32_Bit_q31

  // Notes on the sheet:
  //   I
  //   opcode
  //   rd
  //   rs1
  //   Calculate Immediate
  //   Immediate
  //   en Im
endmodule

module Data_Memory___Control_Buffers (
);

  wire clock_1_out, clock_2_out, Data, Load, LoadL, memEn, not_1_out, or_1_out, Store;
  wire [1:0] Rd, Value;
  wire [3:0] bit_extender_3_out, controlled_buffer_4_out, Rb;
  wire [7:0] Addr;
  wire [15:0] bit_extender_1_out, undriven;
  wire [31:0] bit_extender_2_out, controlled_buffer_1_out, ram_1_data, ram_2_data;

  not not_1 (not_1_out, Load);
  Clock clock_1 (.out(clock_1_out));
  RAM #(.addrWidth(16), .dataWidth(32), .bus("separate")) ram_1 (
    .addr(undriven), .data(ram_1_data), .str(not_1_out), .sel(memEn), .clk(clock_1_out), .ld(Load), .clr(1'b0));  // open: din
  assign bit_extender_1_out = {{8{1'b0}}, Addr};  // Bit_Extender bit_extender_1
  // Probe on ram_1_data
  Clock clock_2 (.out(clock_2_out));
  RAM #(.addrWidth(16), .dataWidth(32), .bus("separate")) ram_2 (
    .addr(bit_extender_1_out), .din(ram_1_data), .data(ram_2_data), .str(Store), .clk(clock_2_out), .ld(Load));  // open: sel, clr
  assign bit_extender_2_out = {{30{1'b0}}, Value};  // Bit_Extender bit_extender_2
  or or_1 (or_1_out, LoadL, Load);
  assign bit_extender_3_out = {{2{1'b0}}, Rd};  // Bit_Extender bit_extender_3
  Controlled_Buffer #(.width(32)) controlled_buffer_1 (.out(controlled_buffer_1_out), .en(Data));  // open: in
  assign controlled_buffer_1_out = Load ? ram_2_data : 32'bz;  // Controlled_Buffer controlled_buffer_2
  assign controlled_buffer_1_out = LoadL ? bit_extender_2_out : 32'bz;  // Controlled_Buffer controlled_buffer_3
  assign controlled_buffer_4_out = or_1_out ? Rb : 4'bz;  // Controlled_Buffer controlled_buffer_4
  assign controlled_buffer_4_out = Data ? bit_extender_3_out : 4'bz;  // Controlled_Buffer controlled_buffer_5

  // Notes on the sheet:
  //   Memory Unit
  //   Mem Data, Hex
  //   Data Memory
  //   Control Buffers
endmodule

// Mem Data
module Memory_Unit (
);

  wire clock_1_out, not_1_out, undriven;
  wire [15:0] bit_extender_1_out, multiplexer_1_out;
  wire [31:0] ram_1_data;

  Bit_Extender #(.in_width(32)) bit_extender_1 (.out(bit_extender_1_out));  // open: in
  // Probe on multiplexer_1_out
  Multiplexer #(.width(16)) multiplexer_1 (.in0(bit_extender_1_out), .out(multiplexer_1_out));  // open: in1, sel, en
  not not_1 (not_1_out, undriven);
  Clock clock_1 (.out(clock_1_out));
  RAM #(.addrWidth(16), .dataWidth(32), .bus("separate")) ram_1 (
    .addr(multiplexer_1_out), .data(ram_1_data), .str(not_1_out), .clk(clock_1_out), .ld(undriven), .clr(1'b0));  // open: din, sel
  // Probe on ram_1_data

  // Notes on the sheet:
  //   Memory Unit
  //   Mem Data, Hex
endmodule
